// Digital circuit control-unit.dig as structural Verilog
module control_unit (
  input  [2:0] in_2,
  output [7:0] out_1
);

  ROM #(.AddrBits(3), .Bits(8)) rom_1 (.A(in_2), .sel(1'b1), .D(out_1));
  // Pins of 1 and 3 bits meet at in_2

  // Notes on the sheet:
  //   contents of rom_1 (hex, n*v repeats v):
  //   82,86,80,87,87,c2,c7,c0
endmodule
